# Fritzing sketch file 13 (saved by Fritzing 0.9.4)
breadboards: 1

parts:
  LED3 = LED - 5mm [color="Red (633nm)" package="5 mm [THT]"]
  Part1 = Arduino Uno (Rev3)
  R2 = Resistor [tolerance=±5% resistance=220 package=THT]
  U1 = POT [package=pot_mammoth]

nets:
  N1: LED3.cathode, R2.Pin_0
  N2: LED3.anode, Part1.D9_PWM
  N3: Part1.A0, U1.A
  N4: Part1.5V, U1.S
  N5: Part1.GND, R2.Pin_1, U1.E
